// Logisim project PerCycleCPU.circ as structural Verilog
module main (
);

  ROM #(.addrWidth(5), .dataWidth(32)) rom_1 ();  // open: addr, data, sel
endmodule

module GRF (
  input  [4:0] ReadReg1,
  input  [4:0] WriteReg,
  input  WriteEn,
  input  [31:0] WriteData,
  input  [4:0] ReadReg2,
  output [31:0] RData1,
  output [31:0] RData2
);

  wire Clk_out;
  wire [7:0] and_1_out_2;
  wire [31:0] _0, _1, _2, _3, _4, _5, _6, _7, _8, _9, _10, _11, _12, _13, _14, _15, _16, _17, _18, _19, _20,
       _21, _22, _23, _24, _25, _26, _27, _28, _29, _30, _31, and_1_out, decoder_1_out0, multiplexer_1_out,
       multiplexer_2_out;

  Clock Clk (.out(Clk_out));
  Decoder #(.select(5), .enable("false")) decoder_1 (
    .out0(decoder_1_out0[0]), .out1(decoder_1_out0[1]), .out2(decoder_1_out0[2]), .out3(decoder_1_out0[3]),
    .out4(decoder_1_out0[4]), .out5(decoder_1_out0[5]), .out6(decoder_1_out0[6]), .out7(decoder_1_out0[7]),
    .out8(decoder_1_out0[8]), .out9(decoder_1_out0[9]), .out10(decoder_1_out0[10]),
    .out11(decoder_1_out0[11]), .out12(decoder_1_out0[12]), .out13(decoder_1_out0[13]),
    .out14(decoder_1_out0[14]), .out15(decoder_1_out0[15]), .out16(decoder_1_out0[16]),
    .out17(decoder_1_out0[17]), .out18(decoder_1_out0[18]), .out19(decoder_1_out0[19]),
    .out20(decoder_1_out0[20]), .out21(decoder_1_out0[21]), .out22(decoder_1_out0[22]),
    .out23(decoder_1_out0[23]), .out24(decoder_1_out0[24]), .out25(decoder_1_out0[25]),
    .out26(decoder_1_out0[26]), .out27(decoder_1_out0[27]), .out28(decoder_1_out0[28]),
    .out29(decoder_1_out0[29]), .out30(decoder_1_out0[30]), .out31(decoder_1_out0[31]), .sel(WriteReg));
  Multiplexer #(.width(32), .enable("false")) multiplexer_1 (
    .in0({32{1'b0}}), .in1({32{1'b1}}), .out(multiplexer_1_out), .sel(Clk_out));
  Multiplexer #(.width(32), .enable("false")) multiplexer_2 (
    .in0({32{1'b0}}), .in1({32{1'b1}}), .out(multiplexer_2_out), .sel(WriteEn));
  assign {and_1_out[31:16], and_1_out_2, and_1_out[7:0]} = decoder_1_out0 & multiplexer_1_out & multiplexer_2_out;  // AND_Gate and_1, 32 bits wide
  Register #(.width(32)) u__0 (.D(WriteData), .en(1'b0), .Q(_0), .clk(and_1_out[0]));  // open: clr
  Register #(.width(32)) u__1 (.D(WriteData), .Q(_1), .clk(and_1_out[1]));  // open: en, clr
  Register #(.width(32)) u__2 (.D(WriteData), .Q(_2), .clk(and_1_out[2]));  // open: en, clr
  Register #(.width(32)) u__3 (.D(WriteData), .Q(_3), .clk(and_1_out[3]));  // open: en, clr
  Register #(.width(32)) u__4 (.D(WriteData), .Q(_4), .clk(and_1_out[4]));  // open: en, clr
  Register #(.width(32)) u__5 (.D(WriteData), .Q(_5), .clk(and_1_out[5]));  // open: en, clr
  Register #(.width(32)) u__6 (.D(WriteData), .Q(_6), .clk(and_1_out[6]));  // open: en, clr
  Register #(.width(32)) u__7 (.D(WriteData), .Q(_7), .clk(and_1_out[7]));  // open: en, clr
  Register #(.width(32)) u__8 (.D(WriteData), .Q(_8), .clk(and_1_out_2[0]));  // open: en, clr
  Register #(.width(32)) u__9 (.D(WriteData), .Q(_9), .clk(and_1_out_2[1]));  // open: en, clr
  Register #(.width(32)) u__10 (.D(WriteData), .Q(_10), .clk(and_1_out_2[2]));  // open: en, clr
  Register #(.width(32)) u__11 (.D(WriteData), .Q(_11), .clk(and_1_out_2[3]));  // open: en, clr
  Register #(.width(32)) u__12 (.D(WriteData), .Q(_12), .clk(and_1_out_2[4]));  // open: en, clr
  Register #(.width(32)) u__13 (.D(WriteData), .Q(_13), .clk(and_1_out_2[5]));  // open: en, clr
  Register #(.width(32)) u__14 (.D(WriteData), .Q(_14), .clk(and_1_out_2[6]));  // open: en, clr
  Register #(.width(32)) u__15 (.D(WriteData), .Q(_15), .clk(and_1_out_2[7]));  // open: en, clr
  Register #(.width(32)) u__16 (.D(WriteData), .Q(_16), .clk(and_1_out[16]));  // open: en, clr
  Register #(.width(32)) u__17 (.D(WriteData), .Q(_17), .clk(and_1_out[17]));  // open: en, clr
  Register #(.width(32)) u__18 (.D(WriteData), .Q(_18), .clk(and_1_out[18]));  // open: en, clr
  Register #(.width(32)) u__19 (.Q(_19), .clk(and_1_out[19]));  // open: D, en, clr
  Register #(.width(32)) u__20 (.D(WriteData), .Q(_20), .clk(and_1_out[20]));  // open: en, clr
  Register #(.width(32)) u__21 (.D(WriteData), .Q(_21), .clk(and_1_out[21]));  // open: en, clr
  Register #(.width(32)) u__22 (.D(WriteData), .Q(_22), .clk(and_1_out[22]));  // open: en, clr
  Register #(.width(32)) u__23 (.D(WriteData), .Q(_23), .clk(and_1_out[23]));  // open: en, clr
  Register #(.width(32)) u__24 (.D(WriteData), .Q(_24), .clk(and_1_out[24]));  // open: en, clr
  Register #(.width(32)) u__25 (.D(WriteData), .Q(_25), .clk(and_1_out[25]));  // open: en, clr
  Register #(.width(32)) u__26 (.D(WriteData), .Q(_26), .clk(and_1_out[26]));  // open: en, clr
  Register #(.width(32)) u__27 (.D(WriteData), .Q(_27), .clk(and_1_out[27]));  // open: en, clr
  Register #(.width(32)) u__28 (.D(WriteData), .Q(_28), .clk(and_1_out[28]));  // open: en, clr
  Register #(.width(32)) u__29 (.D(WriteData), .Q(_29), .clk(and_1_out[29]));  // open: en, clr
  Register #(.width(32)) u__30 (.D(WriteData), .Q(_30), .clk(and_1_out[30]));  // open: en, clr
  Register #(.width(32)) u__31 (.D(WriteData), .Q(_31), .clk(and_1_out[31]));  // open: en, clr
  Multiplexer #(.select(5), .width(32), .enable("false")) multiplexer_3 (
    .in0(_0), .in1(_1), .in2(_2), .in3(_3), .in4(_4), .in5(_5), .in6(_6), .in7(_7), .in8(_8), .in9(_9),
    .in10(_10), .in11(_11), .in12(_12), .in13(_13), .in14(_14), .in15(_15), .in16(_16), .in17(_17),
    .in18(_18), .in19(_19), .in20(_20), .in21(_21), .in22(_22), .in23(_23), .in24(_24), .in25(_25),
    .in26(_26), .in27(_27), .in28(_28), .in29(_29), .in30(_30), .in31(_31), .out(RData1), .sel(ReadReg1));
  Multiplexer #(.select(5), .width(32), .enable("false")) multiplexer_4 (
    .in0(_0), .in1(_1), .in2(_2), .in3(_3), .in4(_4), .in5(_5), .in6(_6), .in7(_7), .in8(_8), .in9(_9),
    .in10(_10), .in11(_11), .in12(_12), .in13(_13), .in14(_14), .in15(_15), .in16(_16), .in17(_17),
    .in18(_18), .in19(_19), .in20(_20), .in21(_21), .in22(_22), .in23(_23), .in24(_24), .in25(_25),
    .in26(_26), .in27(_27), .in28(_28), .in29(_29), .in30(_30), .in31(_31), .out(RData2), .sel(ReadReg2));

  // Other names for the same wires on the sheet: WData[31:0] = WriteData
endmodule

module ALU (
  input  [31:0] A,
  input  [31:0] B,
  input  [1:0] ALUOp,
  output [31:0] Outcome,
  output Zero
);

  wire [31:0] adder_1_out, or_1_out, subtractor_1_out;

  Adder #(.width(32)) adder_1 (.a(A), .b(B), .out(adder_1_out));  // open: cin, cout
  Subtractor #(.width(32)) subtractor_1 (.a(A), .b(B), .out(subtractor_1_out));  // open: bin, bout
  assign or_1_out = A | B;  // OR_Gate or_1, 32 bits wide
  Comparator #(.width(32)) comparator_1 (.a(A), .b(B), .eq(Zero));  // open: gt, lt
  Multiplexer #(.select(2), .width(32), .enable("false")) multiplexer_1 (
    .in0(adder_1_out), .in1(subtractor_1_out), .in2(or_1_out), .out(Outcome), .sel(ALUOp));  // open: in3
endmodule
